# Fritzing sketch Bike's_Pal (saved by Fritzing 0.9.10b)

parts:
  J1 = female pin header, 8 pins [form="♀ (female)"]
  Keypad4x1 = Keypad Membran 4x4
  Part1 = Arduino Uno (Rev3)
  KY-1 = Keyes Relay [package=THT]
  J2 = Piezo Speaker
  SIM800L_BO1 = SIM800L BO
  Power_plug2 = Power plug  # not connected

nets:
  N1: J1.pin1, Keypad4x1.Pin1, Part1.D9_PWM
  N2: J1.pin2, Keypad4x1.Pin2, Part1.D8
  N3: J1.pin3, Keypad4x1.Pin3, Part1.D7
  N4: J1.pin6, Keypad4x1.Pin6, Part1.D4
  N5: J1.pin7, Keypad4x1.Pin7, Part1.D3_PWM
  N6: J1.pin8, Keypad4x1.Pin8, Part1.D2
  N7: Keypad4x1.Pin4, Part1.D6_PWM
  N8: Keypad4x1.Pin5, Part1.D5_PWM
  N9: Part1.D10_PWM/SS, KY-1.power
  N10: Part1.D11_PWM/MOSI, J2.pin2
  N11: Part1.GND, KY-1.ground, SIM800L_BO1.pin_10
  N12: Part1.D0/RX, SIM800L_BO1.pin_6
  N13: Part1.D1/TX, SIM800L_BO1.pin_4
  N14: Part1.5V, KY-1.signal
  N15: Part1.VIN, SIM800L_BO1.pin_12

notes:
  TXD of 800l
  RXD of 800l
  5V ,2Amp Power Supply
  To spark plug

custom parts:
  Keypad Membran 4x4: Membrane Keypad 4x4 Matrix
  Keyes Relay: The Keyes 5V relay module is suitable for SCM development, home appliance control. It uses a 5V~12V TIL control signal which can control DC / AC signal.
